# Fritzing sketch schematic (saved by Fritzing 0.9.3b)
breadboards: 1

parts:
  Raspberry_Pi1 = Raspberry Pi 2
  Part1 = IFR520 MOS module [package=THT]
  PIR1 = PIR sensor
  HLK-PM1 = HLK-PM12 [part_number=HLK-PM12]
  J2 = Power Jack [package=power_jack_smd]
  LED5 = LEDs [package=led-1206]
  LED6 = LEDs [package=led-1206]  # not connected
  LED7 = LEDs [package=led-1206]  # not connected
  LED8 = LEDs [package=led-1206]  # not connected
  J5 = Power Jack [package=power_jack_smd]
  J6 = Power Jack [package=power_jack_smd]
  LED9 = LEDs [package=led-1206]  # not connected
  LED10 = LEDs [package=led-1206]
  LED11 = LEDs [package=led-1206]  # not connected
  LED12 = LEDs [package=led-1206]  # not connected
  J7 = Power Jack [package=power_jack_smd]
  J8 = Power Jack [package=power_jack_smd]

nets:
  N1: Raspberry_Pi1.GPIO23, PIR1.SIG
  N2: Raspberry_Pi1.GPIO18, Part1.SIG
  GND: Raspberry_Pi1.GND, Part1.GND, PIR1.GND, HLK-PM1.-Vo
  5V: Raspberry_Pi1.5V, Part1.VCC, PIR1.VDD
  N3: Part1.V+, J2.GNDBREAK
  N4: Part1.V-, J2.GND
  N5: Part1.VIN, HLK-PM1.+Vo
  N6: J2.PWR, J7.PWR
  N7: LED5.A, J5.GNDBREAK, J6.GNDBREAK
  GND_2: LED5.C, J5.GND, J6.GND
  N8: J6.PWR, J8.PWR
  N9: LED10.A, J7.GNDBREAK, J8.GNDBREAK
  GND_3: LED10.C, J7.GND, J8.GND
